# Fritzing sketch universal_wx (saved by Fritzing 0.9.4)

parts:
  Bauteil1 = Arduino Mega 2560 (Rev3)
  LED3 = LED - 5mm [color="Blue (470nm)" package="5 mm [THT]"]
  LED2 = LED - 5mm [color="Red (635nm)" package="5 mm [THT]"]
  LED1 = LED - 5mm [color="Orange (605nm)" package="5 mm [THT]"]
  BME280 = mystery part, 4 pins [chip_label=BME280]
  SHIFT = mystery part, 8 pins [chip_label=LVLSHFT]
  SI1145 = mystery part, 4 pins [chip_label=SI1145]
  GSM = mystery part, 5 pins [chip_label=GSM]
  U1 = Voltage Regulator - Variable [package="TO220 [THT]"]
  DHT = mystery part, 3 pins [chip_label=DHT11]
  DS = mystery part, 3 pins [chip_label=DS18B20]
  U2 = mystery part, 3 pins [chip_label=NC]
  R1 = Resistor [tolerance=±5% resistance=4.7k package=THT]
  R2 = Resistor [tolerance=±5% resistance=2.2k package=THT]
  R3 = Resistor [tolerance=±5% resistance=1k package=THT]
  C1 = Electrolytic Capacitor [capacitance=470µF package="100 mil [THT, electrolytic]"]
  RAIN = mystery part, 2 pins [chip_label=Rain]
  SPEED = mystery part, 2 pins [chip_label=Speed]
  DIR = mystery part, 2 pins [chip_label=Direction]
  R4 = Resistor [tolerance=±5% resistance=220 package=THT]

nets:
  N1: Bauteil1.A0, DIR.pin1, R4.Pin_1
  N2: Bauteil1.D21/SCL, SHIFT.pin4
  N3: Bauteil1.D20/SDA, SHIFT.pin3
  N4: Bauteil1.D19/RX1, GSM.pin5
  N5: Bauteil1.D18/TX1, GSM.pin4
  N6: Bauteil1.GND, LED3.cathode, LED2.cathode, LED1.cathode, SHIFT.pin2, GSM.pin2, DHT.pin3, DS.pin3, U2.pin3, R2.Pin_1, C1.-, RAIN.pin2, SPEED.pin2, DIR.pin2
  N7: Bauteil1.D13_PWM, LED1.anode
  N8: Bauteil1.D12_PWM, DS.pin2, R1.Pin_1
  N9: Bauteil1.D9_PWM, GSM.pin3
  N10: Bauteil1.D8_PWM, DHT.pin2
  N11: Bauteil1.3V3, BME280.pin1, SHIFT.pin8, SI1145.pin1, U2.pin1
  N12: Bauteil1.5V, SHIFT.pin1, DHT.pin1, DS.pin1, U2.pin2, R1.Pin_0, R4.Pin_0
  N13: Bauteil1.VIN, U1.IN
  N14: Bauteil1.D2_PWM, SPEED.pin1
  N15: Bauteil1.D3_PWM, RAIN.pin1
  N16: Bauteil1.D52, LED3.anode
  N17: Bauteil1.D53, LED2.anode
  N18: BME280.pin2, SHIFT.pin7, SI1145.pin2
  N19: BME280.pin3, SHIFT.pin6, SI1145.pin3
  N20: BME280.pin4, SHIFT.pin5, SI1145.pin4
  N21: GSM.pin1, U1.OUT, R3.Pin_0, C1.+
  N22: U1.ADJ, R2.Pin_0, R3.Pin_1
